// Logisim project ALU(1).circ as structural Verilog: 2 circuits, main circuit 1-Bit ALU
module _1_Bit_ALU (
  input  A,
  input  B,
  input  C2,
  input  C1,
  input  C0,
  output Result,
  output Cout
);

  wire adder_1_cout, adder_1_out, adder_2_cout, adder_2_out, divider_1_out, divider_1_rem, multiplier_1_cout,
       multiplier_1_out, not_1_out, subtractor_1_bout, subtractor_1_out, xor_1_out;

  not not_1 (not_1_out, 1'b0);
  Adder #(.width(1)) adder_1 (.a(A), .b(not_1_out), .out(adder_1_out), .cin(1'b0), .cout(adder_1_cout));
  Adder #(.width(1)) adder_2 (.a(A), .b(B), .out(adder_2_out), .cin(1'b0), .cout(adder_2_cout));
  Subtractor #(.width(1)) subtractor_1 (.a(A), .b(B), .out(subtractor_1_out), .bin(1'b0), .bout(subtractor_1_bout));
  Multiplier #(.width(1)) multiplier_1 (.a(A), .b(B), .out(multiplier_1_out), .cin(1'b0), .cout(multiplier_1_cout));
  Divider #(.width(1)) divider_1 (.a(A), .b(B), .out(divider_1_out), .upper(1'b0), .rem(divider_1_rem));
  xor xor_1 (xor_1_out, A, B);
  Multiplexer #(.select(3), .enable("false")) multiplexer_1 (
    .in0(1'b0), .in1(A), .in2(adder_1_out), .in3(multiplier_1_out), .in4(subtractor_1_out),
    .in5(divider_1_out), .in6(adder_2_out), .in7(xor_1_out), .out(Result), .sel({C2, C1, C0}));
  Multiplexer #(.select(3), .enable("false")) multiplexer_2 (
    .in0(1'b0), .in1(1'b0), .in2(adder_1_cout), .in3(multiplier_1_cout), .in4(subtractor_1_bout),
    .in5(divider_1_rem), .in6(adder_2_cout), .in7(1'b0), .out(Cout), .sel({C2, C1, C0}));
endmodule

module _16_Bit_ALU (
  input  [15:0] A,
  input  [15:0] B,
  input  C2,
  input  C1,
  input  C0,
  output [15:0] Result,
  output [15:0] Cout
);

  wire adder_1_cout, adder_2_cout, bit_extender_1_out, subtractor_1_bout;
  wire [15:0] adder_1_out, adder_2_out, bit_extender_2_out, bit_extender_3_out, bit_extender_4_out,
       bit_extender_5_out, bit_extender_6_out, divider_1_out, divider_1_rem, multiplier_1_cout,
       multiplier_1_out, subtractor_1_out, xor_1_out;

  Bit_Extender #(.in_width(16), .out_width(1)) bit_extender_1 (.in(bit_extender_3_out), .out(bit_extender_1_out));
  assign bit_extender_2_out = {{15{1'b0}}, 1'b1};  // Bit_Extender bit_extender_2
  Adder #(.width(16)) adder_1 (
    .a(A), .b(bit_extender_2_out), .out(adder_1_out), .cin(bit_extender_1_out), .cout(adder_1_cout));
  Adder #(.width(16)) adder_2 (.a(A), .b(B), .out(adder_2_out), .cin(bit_extender_1_out), .cout(adder_2_cout));
  Subtractor #(.width(16)) subtractor_1 (
    .a(A), .b(B), .out(subtractor_1_out), .bin(bit_extender_1_out), .bout(subtractor_1_bout));
  Multiplier #(.width(16)) multiplier_1 (
    .a(A), .b(B), .out(multiplier_1_out), .cin(bit_extender_3_out), .cout(multiplier_1_cout));
  Divider #(.width(16)) divider_1 (.a(A), .b(B), .out(divider_1_out), .upper(bit_extender_3_out), .rem(divider_1_rem));
  assign bit_extender_3_out = {{15{1'b0}}, 1'b0};  // Bit_Extender bit_extender_3
  assign bit_extender_4_out = {{15{1'b0}}, adder_1_cout};  // Bit_Extender bit_extender_4
  assign bit_extender_5_out = {{15{1'b0}}, adder_2_cout};  // Bit_Extender bit_extender_5
  assign bit_extender_6_out = {{15{1'b0}}, subtractor_1_bout};  // Bit_Extender bit_extender_6
  assign xor_1_out = A ^ B;  // XOR_Gate xor_1, 16 bits wide
  Multiplexer #(.select(3), .width(16), .enable("false")) multiplexer_1 (
    .in0(bit_extender_3_out), .in1(A), .in2(adder_1_out), .in3(multiplier_1_out), .in4(subtractor_1_out),
    .in5(divider_1_out), .in6(adder_2_out), .in7(xor_1_out), .out(Result), .sel({C2, C1, C0}));
  Multiplexer #(.select(3), .width(16), .enable("false")) multiplexer_2 (
    .in0(bit_extender_3_out), .in1(bit_extender_3_out), .in2(bit_extender_4_out), .in3(multiplier_1_cout),
    .in4(bit_extender_6_out), .in5(divider_1_rem), .in6(bit_extender_5_out), .in7(bit_extender_3_out),
    .out(Cout), .sel({C2, C1, C0}));
endmodule
