// Logisim project Control Unit.circ as structural Verilog: 1 circuit, main circuit main
module main (
  input  T0,
  input  T1,
  input  T2,
  input  T3,
  input  T4,
  input  T5,
  input  T6,
  input  D0,
  input  D1,
  input  D2,
  input  D3,
  input  D4,
  input  D5,
  input  D6,
  input  [15:0] DR,
  output Decoder_Enable,
  output AR__Load,
  output IR_Load,
  output DR__Load,
  output TR__Load,
  output AC__Load,
  output PC__Load,
  output PC__INC,
  output DR__INC,
  output Memory__read,
  output Memory__Write,
  output SC__Clear,
  output X1__Bus,
  output X2__Bus,
  output X3__Bus,
  output X4__Bus,
  output X5__Bus,
  output X7__Bus,
  output X1__ALU,
  output X3__ALU,
  output X5__ALU,
  output X6__ALU
);

  wire and_1_out, and_2_out, and_3_out, and_4_out, and_5_out, and_6_out, and_7_out, and_8_out, and_10_out,
       and_11_out, and_12_out, and_13_out, and_14_out, and_16_out, and_17_out, and_18_out, and_19_out,
       and_20_out, and_21_out, and_22_out, and_23_out, and_24_out, and_25_out, and_26_out, and_27_out,
       and_28_out, and_29_out, and_31_out, and_32_out, and_35_out, and_36_out, nor_1_out;

  nor nor_1 (nor_1_out, DR[0], DR[1], DR[2], DR[3], DR[4], DR[5], DR[6], DR[7], DR[8], DR[9], DR[10], DR[11], DR[12], DR[13], DR[14], DR[15]);
  and and_1 (and_1_out, D6, T5);
  and and_2 (and_2_out, nor_1_out, and_1_out);
  and and_3 (and_3_out, D0, T3);
  and and_4 (and_4_out, D1, T3);
  and and_5 (and_5_out, D2, T3);
  and and_6 (and_6_out, D5, T3);
  and and_7 (and_7_out, D6, T3);
  and and_8 (and_8_out, D0, T5);
  and and_9 (TR__Load, D0, T4);
  and and_10 (and_10_out, D0, T4);
  and and_11 (and_11_out, D1, T4);
  and and_12 (and_12_out, D2, T4);
  and and_13 (and_13_out, D5, T4);
  and and_14 (and_14_out, D0, T6);
  and and_15 (PC__Load, D4, T3);
  and and_16 (and_16_out, D0, T3);
  and and_17 (and_17_out, D1, T3);
  and and_18 (and_18_out, D2, T3);
  and and_19 (and_19_out, D5, T3);
  and and_20 (and_20_out, D6, T3);
  and and_21 (and_21_out, D3, T3);
  and and_22 (and_22_out, D6, T5);
  and and_23 (and_23_out, D3, T3);
  and and_24 (and_24_out, D4, T3);
  and and_25 (and_25_out, D1, T4);
  and and_26 (and_26_out, D2, T4);
  and and_27 (and_27_out, D5, T4);
  and and_28 (and_28_out, D6, T5);
  and and_29 (and_29_out, D0, T6);
  and and_30 (X1__Bus, D4, T3);
  and and_31 (and_31_out, D3, T3);
  and and_32 (and_32_out, D0, T4);
  and and_33 (X4__Bus, D6, T5);
  and and_34 (X5__Bus, D0, T5);
  and and_35 (and_35_out, D0, T4);
  and and_36 (and_36_out, D2, T4);
  and and_37 (X3__ALU, D5, T4);
  and and_38 (X5__ALU, D0, T6);
  and and_39 (X6__ALU, D1, T4);
  or or_1 (AR__Load, T0, T2);
  or or_2 (PC__INC, T1, and_2_out);
  and and_40 (DR__INC, D6, T4);
  or or_3 (X3__Bus, and_31_out, and_32_out);
  or or_4 (X1__ALU, and_35_out, and_36_out);
  or or_5 (Memory__Write, and_21_out, and_22_out);
  or or_6 (DR__Load, and_3_out, and_4_out, and_5_out, and_6_out, and_7_out, and_8_out);
  or or_7 (AC__Load, and_10_out, and_11_out, and_12_out, and_13_out, and_14_out);
  or or_8 (Memory__read, T1, and_16_out, and_17_out, and_18_out, and_19_out, and_20_out);
  or or_9 (SC__Clear, and_23_out, and_24_out, and_25_out, and_26_out, and_27_out, and_28_out, and_29_out);

  assign Decoder_Enable = T2;
  assign IR_Load = T1;
  assign X2__Bus = T0;
  assign X7__Bus = T2;
endmodule
