// Logisim project Encoder.circ as structural Verilog: 1 circuit, main circuit main
module main (
  input  X1,
  input  X2,
  input  X3,
  input  X4,
  input  X5,
  input  X6,
  input  X7,
  output S0,
  output S1,
  output S2
);

  or or_1 (S0, X1, X3, X5, X7);
  or or_2 (S1, X2, X3, X6, X7);
  or or_3 (S2, X5, X4, X6, X7);
endmodule
