// Logisim project Main Circuit.circ as structural Verilog: 1 circuit, main circuit main
module main (
  input  in_1,
  output [15:0] E
);

  wire AC__Load, AR__Load, CLock, D0, D1, D2, D3, D4, D5, D6, d_ff_1_q, Decoder_Enb, DR__INC, DR__Load,
       IR_Load, main_1_s0, main_1_s1, main_1_s2, Memory__read, Memory__write, n16_bit_alu_1_p6, PC__INC,
       PC__Load, SC__Clear, T0, T1, T2, T3, T4, T5, T6, TR__Load, X1__ALU, X1__BUS, X2__BUS, X3__ALU,
       X3__BUS, X4__BUS, X5__ALU, X5__BUS, X6__ALU, X7__BUS;
  wire [2:0] counter_1_q, main_2_s0;
  wire [6:0] bit_extender_1_out, bit_extender_2_out, PC_p9;
  wire [15:0] AC_OUT, AR_p3, bit_extender_3_out, DR, DR_p2, IR__OUT, ram_1_data, TR_p3;

  Control_Unit_main Control_Unit (
    .T0(T0), .T1(T1), .T2(T2), .T3(T3), .T4(T4), .T5(T5), .T6(T6), .D0(D0), .D1(D1), .D2(D2), .D3(D3),
    .D4(D4), .D5(D5), .D6(D6), .DR(DR), .Decoder_Enable(Decoder_Enb), .AR__Load(AR__Load), .IR_Load(IR_Load),
    .DR__Load(DR__Load), .TR__Load(TR__Load), .AC__Load(AC__Load), .PC__Load(PC__Load), .PC__INC(PC__INC),
    .DR__INC(DR__INC), .Memory__read(Memory__read), .Memory__Write(Memory__write), .SC__Clear(SC__Clear),
    .X1__Bus(X1__BUS), .X2__Bus(X2__BUS), .X3__Bus(X3__BUS), .X4__Bus(X4__BUS), .X5__Bus(X5__BUS),
    .X7__Bus(X7__BUS), .X1__ALU(X1__ALU), .X3__ALU(X3__ALU), .X5__ALU(X5__ALU), .X6__ALU(X6__ALU));
  Clock clock_1 (.out(CLock));
  Bit_Extender #(.in_width(16), .out_width(7)) bit_extender_1 (.in(DR_p2), .out(bit_extender_1_out));
  // Modified_Register_main DR: pin names not known; wires that end beside it: DR__Load, DR_p2, CLock, 1'b0, DR__INC, DR
  Encoder_main main_1 (
    .X1(X1__ALU), .X2(1'b0), .X3(X3__ALU), .X4(1'b0), .X5(X5__ALU), .X6(X6__ALU), .X7(1'b0), .S0(main_1_s0),
    .S1(main_1_s1), .S2(main_1_s2));
  // Modified_Register_main AR: pin names not known; wires that end beside it: AR__Load, DR_p2, AR_p3
  // Modified_Counter_main PC: pin names not known; wires that end beside it: PC__Load, bit_extender_1_out, CLock, CLock, 1'b0, 1'b0, 1'b0, PC__INC, PC_p9
  // Modified_Register_main TR: pin names not known; wires that end beside it: TR__Load, DR_p2, TR_p3
  // Modified_Register_main IR: pin names not known; wires that end beside it: IR_Load, DR_p2, CLock, CLock, 1'b0, 1'b0, 1'b0, 1'b0, IR__OUT
  Decoder #(.select(3), .enable("false")) decoder_1 (
    .out0(D0), .out1(D1), .out2(D2), .out3(D3), .out4(D4), .out5(D5), .out6(D6), .sel(IR__OUT[14:12]));  // open: out7
  Bit_Extender #(.in_width(16), .out_width(7)) bit_extender_2 (.in(AR_p3), .out(bit_extender_2_out));
  assign bit_extender_3_out = {{9{1'b0}}, PC_p9};  // Bit_Extender bit_extender_3
  // _16_Bit_ALU 16_bit_alu_1: pin names not known; wires that end beside it: DR, AC_OUT, main_1_s2, main_1_s1, main_1_s0, n16_bit_alu_1_p6, E
  RAM #(.addrWidth(7), .dataWidth(16), .bus("separate")) ram_1 (
    .addr(bit_extender_2_out), .din(DR_p2), .data(ram_1_data), .str(Memory__write), .clk(CLock),
    .ld(Memory__read));  // open: sel, clr
  // Modified_Register_main AC: pin names not known; wires that end beside it: AC__Load, n16_bit_alu_1_p6, CLock, 1'b0, 1'b0, AC_OUT
  Counter #(.width(3), .max('h7)) counter_1 (
    .load(in_1), .count(1'b1), .Q(counter_1_q), .clk(CLock), .clr(d_ff_1_q));  // open: D, carry
  D_Flip_Flop d_ff_1 (.clk(CLock), .D(SC__Clear), .Q(d_ff_1_q));  // open: Qn, preset, en, reset
  Encoder_main main_2 (
    .X1(X1__BUS), .X2(X2__BUS), .X3(X3__BUS), .X4(X4__BUS), .X5(X5__BUS), .X6(1'b0), .X7(X7__BUS),
    .S0(main_2_s0[0]), .S1(main_2_s0[1]), .S2(main_2_s0[2]));
  Decoder #(.select(3), .enable("false")) decoder_2 (
    .out1(T0), .out2(T1), .out3(T2), .out4(T3), .out5(T4), .out6(T5), .out7(T6), .sel(counter_1_q));  // open: out0
  Multiplexer #(.select(3), .width(16), .enable("false")) multiplexer_1 (
    .in0(ram_1_data), .in1(AR_p3), .in2(bit_extender_3_out), .in3(AC_OUT), .in4(DR), .in5(TR_p3),
    .in7(IR__OUT), .out(DR_p2), .sel(main_2_s0));  // open: in6
endmodule
