// Logisim project Modified Counter(1).circ as structural Verilog: 1 circuit, main circuit main
module main (
  input  in_1,
  input  [6:0] in_2,
  input  in_3,
  input  in_4,
  input  in_5,
  output [6:0] out_6
);

  wire d_ff_1_q;

  Counter #(.width(7), .max('h7f)) counter_1 (
    .load(in_1), .D(in_2), .count(in_3), .Q(out_6), .clk(in_4), .clr(d_ff_1_q));  // open: carry
  D_Flip_Flop d_ff_1 (.clk(in_4), .D(in_5), .Q(d_ff_1_q));  // open: Qn, preset, en, reset
endmodule
