// Logisim project Modified Register(1).circ as structural Verilog: 1 circuit, main circuit main
module main (
  input  [15:0] in_1,
  input  in_2,
  input  in_3,
  input  in_4,
  input  in_5,
  output [15:0] out_6
);

  wire d_ff_1_q, or_1_out;
  wire [15:0] adder_1_out, multiplexer_1_out;

  Adder #(.width(16)) adder_1 (.a(out_6), .b(16'h1), .out(adder_1_out), .cin(1'b0));  // open: cout
  or or_1 (or_1_out, in_2, in_3);
  Multiplexer #(.width(16), .enable("false")) multiplexer_1 (
    .in0(in_1), .in1(adder_1_out), .out(multiplexer_1_out), .sel(in_2));
  D_Flip_Flop d_ff_1 (.clk(in_4), .D(in_5), .Q(d_ff_1_q));  // open: Qn, preset, en, reset
  Register #(.width(16)) register_1 (.D(multiplexer_1_out), .en(or_1_out), .Q(out_6), .clk(in_4), .clr(d_ff_1_q));
endmodule
