// Logisim project SC.circ as structural Verilog: 1 circuit, main circuit main
module main (
  input  in_1,
  input  in_2,
  output [2:0] out_3
);

  wire d_ff_1_q;

  Counter #(.width(3), .max('h7)) counter_1 (.Q(out_3), .clk(in_1), .clr(d_ff_1_q));  // open: load, D, count, carry
  D_Flip_Flop d_ff_1 (.clk(in_1), .D(in_2), .Q(d_ff_1_q));  // open: Qn, preset, en, reset
endmodule
